# Fritzing sketch ledblink (saved by Fritzing 0.9.0b)
breadboards: 1

parts:
  U1 = attiny85 [package=dip]
  R1 = Resistor [tolerance=±5% resistance=220 package="0603 [SMD]"]
  LED1 = LED - 5mm [color="Red (633nm)" package="5 mm [THT]"]

nets:
  N1: U1.Pin_3, R1.Pin_1
  GND: U1.Pin_4, LED1.cathode
  5V: U1.Pin_8
  N2: R1.Pin_0, LED1.anode
